# Fritzing sketch accd (saved by Fritzing 0.9.3b)
breadboards: 1

parts:
  元件1 = Arduino Nano (Rev3.0)
  U2 = SUP500F [package=sup500f]
  Grove2 = Grove OLED 128x96
  元件2 = u-blox NEO-6M GPS Breakout
  Grove3 = Grove Dust Sensor

nets:
  N1: 元件1.D1/TX, U2.TX-O
  N2: 元件1.D0/RX, U2.RX-I
  GND: 元件1.GND, U2.GND, Grove2.GND, 元件2.GND, Grove3.GND
  N3: 元件1.D4, Grove2.SDA
  N4: 元件1.D5, Grove2.SCL
  N5: 元件1.D10, Grove3.SIG
  5V: 元件1.5V, Grove3.VCC
  N6: 元件1.A7, 元件2.TXD
  N7: 元件1.A2, 元件2.RXD
  VCC: 元件1.3V3, U2.VCC, Grove2.VCC, 元件2.VCC

custom parts:
  Grove Dust Sensor: PPD42 Grove Dust Sensor
