# Fritzing sketch twizy1 (saved by Fritzing 0.9.3b)
breadboards: 1

parts:
  J1 = STM32 Nucleo shields
  元件1 = u-blox NEO-6M GPS Breakout
  Grove1 = Grove Dust Sensor
  元件2 = Adafruit SHT31-D Sensirion Temperature/Humidity Sensor [part_number="Adafruit #2857"]

nets:
  GND: J1.GND, 元件1.GND, Grove1.GND, 元件2.GND
  3V3: J1.3v3, 元件1.VCC
  5V: J1.5V, Grove1.VCC, 元件2.VIN
  N1: J1.PA6, 元件2.SDA
  N2: J1.PA7, 元件2.SCL
  N3: J1.PB6, Grove1.SIG
  N4: J1.PA9, 元件1.TXD
  N5: J1.PA10, 元件1.RXD

custom parts:
  STM32 Nucleo shields: Clownface.space shield blank for STM32 NUCLEO-64 boards. Morpho pins only.
  Grove Dust Sensor: PPD42 Grove Dust Sensor
  Adafruit SHT31-D Sensirion Temperature/Humidity Sensor: Sensirion Temperature/Humidity sensors are some of the finest & highest-accuracy devices you can get. And, finally we have some that have a true I2C interface for easy reading. The SHT31-D sensor has an excellent ±2% relative humidity and ±0.3°C accuracy for most uses. Unlike earlier SHT sensors, this sensor has a true I2C interface, and (bonus!) even with two address options. It also is 3V or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
